// Logisim project practice9.circ as structural Verilog: 1 circuit, main circuit main
module main (
  input  not_S,
  input  S,
  input  C,
  input  R,
  input  not_R,
  input  S_2,
  input  D,
  input  C_2,
  input  not_R_2,
  input  not_S_2,
  input  C_3,
  input  not_R_3,
  input  not_S_3,
  input  J,
  input  C_4,
  input  K,
  input  not_R_4,
  output Q,
  output nQ,
  output Q_2,
  output nQ_2,
  output Q_3,
  output nQ_3,
  output Q_4,
  output nQ_4
);

  wire nand_1_out, nand_2_out, nand_3_out, nand_4_out, nand_5_out, nand_6_out, nand_7_out, nand_8_out,
       nand_9_out, nand_10_out, nand_11_out, nand_12_out, nand_13_out, nand_14_out, nand_15_out, nand_16_out,
       nand_17_out, nand_18_out, nand_19_out, nand_20_out, nand_21_out, nand_22_out, nand_23_out,
       nand_24_out, nand_25_out, nand_26_out, nand_27_out;

  nand nand_1 (nand_1_out, C, C);
  nand nand_2 (nand_2_out, C_2, C_2);
  nand nand_3 (nand_3_out, C_3, C_3);
  nand nand_4 (nand_4_out, nQ_4, J, C_4);
  nand nand_5 (nand_5_out, C_4, K, Q_4);
  nand nand_6 (nand_6_out, S, nand_1_out);
  nand nand_7 (nand_7_out, nand_1_out, R);
  nand nand_8 (nand_8_out, D, nand_2_out);
  nand nand_9 (nand_9_out, nand_2_out, nand_8_out);
  nand nand_10 (nand_10_out, nQ_3, nand_3_out);
  nand nand_11 (nand_11_out, nand_3_out, Q_3);
  nand nand_12 (nand_12_out, not_S_3, nand_4_out, nand_13_out);
  nand nand_13 (nand_13_out, nand_12_out, nand_5_out, not_R_4);
  nand nand_14 (nand_14_out, not_S, nand_6_out, nand_15_out);
  nand nand_15 (nand_15_out, nand_14_out, nand_7_out, not_R);
  nand nand_16 (nand_16_out, S_2, nand_8_out, nand_17_out);
  nand nand_17 (nand_17_out, nand_16_out, nand_9_out, not_R_2);
  nand nand_18 (nand_18_out, not_S_2, nand_10_out, nand_19_out);
  nand nand_19 (nand_19_out, nand_18_out, nand_11_out, not_R_3);
  nand nand_20 (nand_20_out, nand_4_out, nand_12_out, nand_5_out);
  nand nand_21 (nand_21_out, nand_5_out, nand_13_out, nand_4_out);
  nand nand_22 (nand_22_out, nand_14_out, C);
  nand nand_23 (nand_23_out, C, nand_15_out);
  nand nand_24 (nand_24_out, nand_16_out, C_2);
  nand nand_25 (nand_25_out, C_2, nand_17_out);
  nand nand_26 (nand_26_out, nand_18_out, C_3);
  nand nand_27 (nand_27_out, C_3, nand_19_out);
  nand nand_28 (Q_4, not_S_3, nand_20_out, nQ_4);
  nand nand_29 (nQ_4, Q_4, nand_21_out, not_R_4);
  nand nand_30 (Q, not_S, nand_22_out, nQ);
  nand nand_31 (nQ, Q, nand_23_out, not_R);
  nand nand_32 (Q_2, S_2, nand_24_out, nQ_2);
  nand nand_33 (nQ_2, Q_2, nand_25_out, not_R_2);
  nand nand_34 (Q_3, not_S_2, nand_26_out, nQ_3);
  nand nand_35 (nQ_3, Q_3, nand_27_out, not_R_3);

  // Notes on the sheet:
  //   Синхронный фронтовой RS-триггер с асинхронным управлением
  //   Синхронный фронтовой D-триггер с асинхронным управлением
  //   Синхронный фронтовой T-триггер с асинхронным управлением
  //   Синхронный фронтовой JK-триггер с асинхронным управлением
endmodule
